# Fritzing sketch Панель управления квариума (saved by Fritzing 0.9.4)

parts:
  Часть1 = Arduino Pro Mini v13
  JP1 = Header 5 [package=1x05-1mm-ra]
  JP2 = Header 5 [package=1x05-1mm-ra]
  Часть2 = Arduino Nano (Rev3.0) (ICSP)
  X1 = USB Connectors [package=usb-a-s-silk-female]  # not connected
  U2 = 74HC595 SMD [package="SO16 [SMD]"]
  R1 = Resistor [tolerance=±5% resistance=200 package=THT]
  R2 = Resistor [tolerance=±5% resistance=200 package=THT]
  R3 = Resistor [tolerance=±5% resistance=200 package=THT]
  R4 = Resistor [tolerance=±5% resistance=200 package=THT]
  R5 = Resistor [tolerance=±5% resistance=200 package=THT]
  R6 = Resistor [tolerance=±5% resistance=200 package=THT]
  R7 = Resistor [tolerance=±5% resistance=200 package=THT]
  R8 = Resistor [tolerance=±5% resistance=200 package=THT]
  U3 = 74HC595 SMD [package="SO16 [SMD]"]
  R9 = Resistor [tolerance=±5% resistance=200 package=THT]
  R10 = Resistor [tolerance=±5% resistance=200 package=THT]
  R11 = Resistor [tolerance=±5% resistance=200 package=THT]
  R12 = Resistor [tolerance=±5% resistance=200 package=THT]
  R13 = Resistor [tolerance=±5% resistance=200 package=THT]
  R14 = Resistor [tolerance=±5% resistance=200 package=THT]
  R15 = Resistor [tolerance=±5% resistance=200 package=THT]
  R16 = Resistor [tolerance=±5% resistance=200 package=THT]
  Q1 = NPN-Transistor [package="TO92 [THT]"]
  Q2 = NPN-Transistor [package="TO92 [THT]"]
  Q3 = NPN-Transistor [package="TO92 [THT]"]
  S1 = Pushbutton [package="[THT]"]
  S2 = Pushbutton [package="[THT]"]
  RE1 = Rotary Encoder [package=THT]
  R17 = Photocell (LDR) [package=THT]
  R18 = Resistor [tolerance=±5% resistance=10k package=THT]  # not connected
  R19 = Resistor [tolerance=±5% resistance=10k package=THT]  # not connected
  R20 = Resistor [tolerance=±5% resistance=10k package=THT]  # not connected
  R21 = Resistor [tolerance=±5% resistance=10k package=THT]
  R22 = Resistor [tolerance=±5% resistance=10k package=THT]
  R23 = Resistor [tolerance=±5% resistance=10k package=THT]
  C1 = Ceramic Capacitor [capacitance=100nF package="100 mil [THT, multilayer]"]
  R24 = Resistor [tolerance=±5% resistance=10k package=THT]
  C2 = Ceramic Capacitor [capacitance=100nF package="100 mil [THT, multilayer]"]
  R26 = Resistor [tolerance=±5% resistance=10k package=THT]

nets:
  N1: Часть1.D1/RX, JP2.2
  VCC: Часть1.VCC, JP2.1, U3.VCC
  N2: Часть1.A0, R17.pin_0, R23.Pin_1
  N3: Часть1.D12/MISO, R26.Pin_1
  N4: Часть1.D10_PWM/SS, R24.Pin_1
  N5: Часть1.D9_PWM, Q3.C
  N6: Часть1.D8, S2.Pin_3, S2.Pin_4
  N7: Часть1.D7, S1.Pin_3
  N8: Часть1.D6_PWM, Q2.C
  N9: Часть1.D5_PWM, Q1.B, Q1.C
  N10: Часть1.D4, U2.SH_CP
  N11: Часть1.D3_PWM, U2.ST_CP
  N12: Часть1.D2, U2.DS
  N13: JP1.1, Часть2.D0/RX
  N14: JP1.2, Часть2.GND
  N15: Часть2.5V, Часть2.A7
  N16: U2.Q1, R2.Pin_1
  N17: U2.Q2, R3.Pin_1
  N18: U2.Q3, R4.Pin_1
  N19: U2.Q4, R5.Pin_1
  N20: U2.Q5, R8.Pin_0
  N21: U2.Q6, R7.Pin_0
  N22: U2.Q7, R6.Pin_0
  N23: U2.Q7', U3.DS
  N24: U2.Q0, R1.Pin_1
  N25: U3.Q1, R15.Pin_1
  N26: U3.Q2, R14.Pin_1
  N27: U3.Q3, R16.Pin_1
  N28: U3.Q4, R12.Pin_1
  N29: U3.Q5, R11.Pin_0
  N30: U3.Q6, R10.Pin_0
  N31: U3.Q7, R13.Pin_0
  N32: U3.Q0, R9.Pin_1
  N33: RE1.EncoderPinA, R24.Pin_0
  N34: RE1.EncoderPinB, R26.Pin_0
  N35: R21.Pin_1, R22.Pin_1
  N36: C1.1, C2.0

notes:
  200 Ом
  pin 2 (DATA) зеленый
  pin 3 (LATCH) белый
  pin 4 (CLOCK) оранжевый
  Транзисторы NPN
  2N2222 например
  резисторы 10кОм
  резисторы 10кОм
  конденсаторы 100n
  1-10 кОм
