# Fritzing sketch Сервер регулирования и управления аквариумом (saved by Fritzing 0.9.3b)

parts:
  Power_plug1 = Power plug
  Power_plug2 = Power plug  # not connected
  Часть1 = Arduino Pro Mini v13
  M1 = RioRand LM2596
  Power_plug3 = Power plug  # not connected
  U2 = RELAY-SOLIDSTATE [package=relay-s108t02]  # not connected
  C1 = Electrolytic Capacitor [capacitance=100µF voltage=16V package="100 mil [THT, electrolytic]"]  # not connected
  Часть2 = Arduino Nano (Rev3.0) (ICSP)
  Power_plug8 = Power plug
  Q1 = MOSFET-NCHANNEL [package=to220v]
  R1 = Resistor [tolerance=±5% resistance=100 package=THT]
  R2 = Resistor [tolerance=±5% resistance=10k package=THT]
  DS1 = DS18B20 1-Wire Temperature Sensor [part_number=DS18B20]
  DS3 = DS18B20 1-Wire Temperature Sensor [part_number=DS18B20]
  J1 = Dagu DGServo 9g header connector (female) [package=THT]
  J2 = Dagu DGServo 9g header connector (female) [package=THT]
  J3 = Dagu DGServo 9g header connector (female) [package=THT]
  J4 = Dagu DGServo 9g header connector (female) [package=THT]
  R3 = Resistor [tolerance=±5% resistance=4.7k package=THT]  # not connected
  JP1 = Header 5 [package=1x05-1mm-ra]
  JP2 = Header 5 [package=1x05-1mm-ra]

nets:
  VCC: Power_plug1.VCC, M1.Pin_1, Power_plug8.VCC
  N1: Power_plug1.GND, M1.Pin_2, Q1.S, R2.Pin_1
  N2: Часть1.D1/RX, JP2.2
  N3: Часть1.GND, JP2.1
  N4: Часть1.A3, Часть1.A2
  N5: M1.Pin_3, Часть2.5V, J3.pulse, J4.pulse, JP1.2
  GND: M1.Pin_4, Часть2.GND, J3.gnd, J4.gnd
  N6: Часть2.D1/TX, JP1.1
  N7: Часть2.D3, R1.Pin_0
  VCC_2: Часть2.D4, J3.Vcc, J4.Vcc
  N8: Power_plug8.GND, Q1.D
  N9: Q1.G, R1.Pin_1, R2.Pin_0
  GND_2: DS1.GND, J1.gnd
  N10: DS1.DQ, J1.Vcc
  N11: DS1.VDD, J1.pulse
  GND_3: DS3.GND, J2.gnd
  N12: DS3.DQ, J2.Vcc
  N13: DS3.VDD, J2.pulse

notes:
  Источник питания 12V
  ~220V
  pin2
  100мкФ
  понижаем с 12В до 5В
  10кОм
  100 Ом
  MOSFET N-канальный
  IRF3704ZPBF, IRLB8743PBF, IRL2203NIRLB8748PBF, IRL8113PBF, IRL3803PBF, IRLB3813PBF, IRL3502PBF, IRL2505PBF, IRF3711PBF, IRL3713PBF, IRF3709ZPBF, AUIRL3705N, IRLB3034PBF, IRF3711ZPBF, IRF744N
  pin3
  4,7 кОм
  pin4
